# Fritzing sketch circuit (saved by Fritzing 0.9.3b)
breadboards: 1

parts:
  R1 = Resistor [tolerance=±5% resistance=10 package=THT]
  S1 = Pushbutton [package="[THT]"]
  Mojo1 = Embedded Micro Mojo v3

nets:
  N1: R1.Pin_0, S1.Pin_1, S1.Pin_2, Mojo1.50
  N2: R1.Pin_1, Mojo1.GND
  N3: S1.Pin_3, S1.Pin_4, Mojo1.V+

custom parts:
  Embedded Micro Mojo v3: The Mojo is a FPGA development board that is designed from the ground up to be easy to use. The entire goal of the Mojo is to make getting started with FPGA and digital design as easy as possible. To go along with our board, Embedded Micro has tutorials to help you get started and expand your knowledge of digital design. The Mojo is made in the USA. The Mojo features include: Spartan 6 XC6SLX9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
